// Logisim project port_dekoder.circ as structural Verilog: 1 circuit, main circuit main
module main (
  input  nDI_ULA,
  input  nRD,
  input  nWR,
  input  nIORQ,
  input  A1,
  input  A0,
  input  DI_32765,
  input  A7,
  input  A5,
  input  nM1,
  input  A14,
  input  A15,
  output nIN254,
  output nOUT254,
  output CLK_32765,
  output BC1,
  output BDIR
);

  wire buffer_1_out, I1_out, I2_out, I3_out, I4_out, I5_out, I9_out, I11_out, I13_out, I14_out, I15_out,
       I16_out, nand_1_out, nand_2_out, nor_1_out, or_1_out, or_4_out, or_5_out, or_6_out;

  buf I16 (I16_out, nDI_ULA);
  buf I14 (I14_out, nRD);
  buf I13 (I13_out, nWR);
  buf buffer_1 (buffer_1_out, nIORQ);
  buf I5 (I5_out, A1);
  buf I4 (I4_out, A0);
  buf I3 (I3_out, DI_32765);
  buf I11 (I11_out, A7);
  buf I9 (I9_out, A5);
  buf I15 (I15_out, nM1);
  buf I1 (I1_out, A14);
  buf I2 (I2_out, A15);
  or or_1 (or_1_out, I16_out, I4_out, buffer_1_out, ~I11_out, ~I9_out, ~I5_out);  // OR_Gate
  or or_2 (nIN254, I14_out, or_1_out);
  or or_3 (nOUT254, I13_out, or_1_out);
  or or_4 (or_4_out, I5_out, I2_out, ~I4_out, ~I1_out);  // OR_Gate
  or or_5 (or_5_out, I3_out, buffer_1_out, I13_out);
  or or_6 (or_6_out, ~I11_out, ~I9_out);  // OR_Gate
  nor nor_1 (nor_1_out, ~I9_out, ~I11_out, I5_out, buffer_1_out);  // NOR_Gate
  nor nor_2 (CLK_32765, or_4_out, or_5_out, or_6_out);
  nand nand_1 (nand_1_out, I15_out, I1_out);
  nand nand_2 (nand_2_out, nor_1_out, I2_out);
  nor nor_3 (BC1, nand_1_out, nand_2_out);
  nor nor_4 (BDIR, nand_2_out, I13_out);
endmodule
